// Logisim project APS relogio pendentre display.circ as structural Verilog: 7 circuits, main circuit CLOCK INICIAL
module CLOCK_INICIAL (
  input  PINO_RESET,
  output S___A,
  output S___B,
  output S___C,
  output S___D,
  output CX_1
);

  wire CLOCK_DE_CONTAGEM_out, d_ff_1_q, d_ff_2_q, d_ff_3_q, d_ff_4_q, RESET_PELA_PORTA_out;

  Clock CLOCK_DE_CONTAGEM (.out(CLOCK_DE_CONTAGEM_out));
  and RESET_PELA_PORTA (RESET_PELA_PORTA_out, ~S___A, S___B, ~S___C, S___D);  // AND_Gate
  Multiplexer multiplexer_1 (.in0(RESET_PELA_PORTA_out), .in1(PINO_RESET), .out(CX_1));  // open: sel, en
  D_Flip_Flop d_ff_1 (.clk(CLOCK_DE_CONTAGEM_out), .D(S___A), .Q(d_ff_1_q), .preset(CX_1));  // open: Qn, en, reset
  D_Flip_Flop d_ff_2 (.clk(d_ff_1_q), .D(S___B), .Q(d_ff_2_q), .preset(CX_1));  // open: Qn, en, reset
  D_Flip_Flop d_ff_3 (.clk(d_ff_2_q), .D(S___C), .Q(d_ff_3_q), .preset(CX_1));  // open: Qn, en, reset
  D_Flip_Flop d_ff_4 (.clk(d_ff_3_q), .D(S___D), .Q(d_ff_4_q), .preset(CX_1));  // open: Qn, en, reset
  not not_1 (S___A, d_ff_1_q);
  not not_2 (S___B, d_ff_2_q);
  not not_3 (S___C, d_ff_3_q);
  not not_4 (S___D, d_ff_4_q);
endmodule

module CLOCK_0_9 (
  input  CLCOCK,
  input  PINO_RESET,
  output S___A,
  output S___B,
  output S___C,
  output S___D,
  output CX_1
);

  wire d_ff_1_q, d_ff_2_q, d_ff_3_q, d_ff_4_q, RESET_PELA_PORTA_out;

  and RESET_PELA_PORTA (RESET_PELA_PORTA_out, ~S___A, S___B, ~S___C, S___D);  // AND_Gate
  Multiplexer multiplexer_1 (.in0(RESET_PELA_PORTA_out), .in1(PINO_RESET), .out(CX_1));  // open: sel, en
  D_Flip_Flop d_ff_1 (.clk(CLCOCK), .D(S___A), .Q(d_ff_1_q), .preset(CX_1));  // open: Qn, en, reset
  D_Flip_Flop d_ff_2 (.clk(d_ff_1_q), .D(S___B), .Q(d_ff_2_q), .preset(CX_1));  // open: Qn, en, reset
  D_Flip_Flop d_ff_3 (.clk(d_ff_2_q), .D(S___C), .Q(d_ff_3_q), .preset(CX_1));  // open: Qn, en, reset
  D_Flip_Flop d_ff_4 (.clk(d_ff_3_q), .D(S___D), .Q(d_ff_4_q), .preset(CX_1));  // open: Qn, en, reset
  not not_1 (S___A, d_ff_1_q);
  not not_2 (S___B, d_ff_2_q);
  not not_3 (S___C, d_ff_3_q);
  not not_4 (S___D, d_ff_4_q);
endmodule

module CLOCK_0_5 (
  input  CLOCK,
  input  PINO_RESET,
  output S___A,
  output S___B,
  output S___C,
  output CX_1
);

  wire d_ff_1_q, d_ff_2_q, d_ff_3_q, RESET_PELA_PORTA_out;

  and RESET_PELA_PORTA (RESET_PELA_PORTA_out, S___A, S___B, S___C);
  Multiplexer multiplexer_1 (.in0(RESET_PELA_PORTA_out), .in1(PINO_RESET), .out(CX_1));  // open: sel, en
  D_Flip_Flop d_ff_1 (.clk(CLOCK), .D(S___A), .Q(d_ff_1_q), .preset(CX_1));  // open: Qn, en, reset
  D_Flip_Flop d_ff_2 (.clk(d_ff_1_q), .D(S___B), .Q(d_ff_2_q), .preset(CX_1));  // open: Qn, en, reset
  D_Flip_Flop d_ff_3 (.clk(d_ff_2_q), .D(S___C), .Q(d_ff_3_q), .preset(CX_1));  // open: Qn, en, reset
  not not_1 (S___A, d_ff_1_q);
  not not_2 (S___B, d_ff_2_q);
  not not_3 (S___C, d_ff_3_q);
endmodule

module relogio (
  input  in_1
);

  CLOCK_0_9 CK_0_9 ();  // open: CLCOCK, PINO_RESET, S___A, S___B, S___C, S___D, CX_1
  CLOCK_INICIAL CK_I ();  // open: PINO_RESET, S___A, S___B, S___C, S___D, CX_1
  ds ds_1 (.a(in_1));  // open: g, f, b, e, d, c
  CLOCK_0_5 CK_0_5 ();  // open: CLOCK, PINO_RESET, S___A, S___B, S___C, CX_1
endmodule

module DISPLAY (
);

  Multiplexer #(.select(4)) multiplexer_1 ();  // open: in0, in1, in2, in3, in4, in5, in6, in7, in8, in9, in10, in11, in12, in13, in14, in15, out, sel, en
  _7_Segment_Display u_7_segment_display_1 ();  // open: g, f, a, b, e, d, c, dp
endmodule

module DECODIFICADOR_BCD_8421_P_7 (
  input  A,
  input  B,
  input  C,
  input  D,
  output a_2,
  output b_2,
  output c_2,
  output d_2,
  output e,
  output f,
  output g
);

  wire and_1_out, and_2_out, and_3_out, and_4_out, and_5_out, and_6_out, and_7_out, and_8_out, and_9_out,
       and_10_out, and_11_out, and_12_out, and_13_out, and_14_out, and_15_out, and_16_out, and_17_out,
       not_1_out, not_2_out, not_3_out, not_4_out, not_5_out, not_6_out, not_7_out, not_8_out, not_9_out,
       not_10_out, not_11_out, not_12_out, not_13_out, not_14_out, not_15_out, not_16_out, not_17_out,
       not_18_out, not_19_out, not_20_out, not_21_out, or_1_out, or_2_out, or_3_out, or_4_out, or_6_out,
       or_8_out, or_9_out, or_10_out, or_11_out, or_14_out, or_15_out;

  not not_1 (not_1_out, B);
  and and_1 (and_1_out, not_1_out, not_2_out);
  not not_2 (not_2_out, D);
  and and_2 (and_2_out, B, D);
  not not_3 (not_3_out, B);
  not not_4 (not_4_out, C);
  and and_3 (and_3_out, not_4_out, not_5_out);
  not not_5 (not_5_out, D);
  not not_6 (not_6_out, C);
  or or_1 (or_1_out, not_6_out, D);
  not not_7 (not_7_out, B);
  and and_4 (and_4_out, not_7_out, not_8_out);
  not not_8 (not_8_out, D);
  not not_9 (not_9_out, B);
  and and_5 (and_5_out, not_9_out, C);
  not not_10 (not_10_out, D);
  and and_6 (and_6_out, B, not_11_out);
  not not_11 (not_11_out, C);
  not not_12 (not_12_out, B);
  and and_7 (and_7_out, not_12_out, not_13_out);
  not not_13 (not_13_out, D);
  and and_8 (and_8_out, C, not_14_out);
  not not_14 (not_14_out, D);
  not not_15 (not_15_out, C);
  and and_9 (and_9_out, not_15_out, not_16_out);
  not not_16 (not_16_out, D);
  and and_10 (and_10_out, B, not_17_out);
  not not_17 (not_17_out, C);
  and and_11 (and_11_out, B, not_18_out);
  not not_18 (not_18_out, D);
  not not_19 (not_19_out, B);
  and and_12 (and_12_out, not_19_out, C);
  and and_13 (and_13_out, B, not_20_out);
  not not_20 (not_20_out, C);
  and and_14 (and_14_out, B, not_21_out);
  not not_21 (not_21_out, D);
  or or_2 (or_2_out, and_1_out, C);
  or or_3 (or_3_out, and_2_out, A);
  or or_4 (or_4_out, not_3_out, and_3_out);
  and and_15 (and_15_out, C, D);
  or or_5 (c_2, or_1_out, B);
  or or_6 (or_6_out, and_4_out, and_5_out);
  and and_16 (and_16_out, C, not_10_out);
  and and_17 (and_17_out, and_6_out, D);
  or or_7 (e, and_7_out, and_8_out);
  or or_8 (or_8_out, and_9_out, and_10_out);
  or or_9 (or_9_out, and_11_out, A);
  or or_10 (or_10_out, and_12_out, and_13_out);
  or or_11 (or_11_out, and_14_out, A);
  or or_12 (a_2, or_2_out, or_3_out);
  or or_13 (b_2, or_4_out, and_15_out);
  or or_14 (or_14_out, or_6_out, and_16_out);
  or or_15 (or_15_out, and_17_out, A);
  or or_16 (f, or_8_out, or_9_out);
  or or_17 (g, or_10_out, or_11_out);
  or or_18 (d_2, or_14_out, or_15_out);
endmodule

module ds (
  input  g,
  input  f,
  input  a,
  input  b,
  input  e,
  input  d,
  input  c
);

  _7_Segment_Display u_7_segment_display_1 (.g(g), .f(f), .a(a), .b(b), .e(e), .d(d), .c(c));  // open: dp
endmodule
