// Logisim project relogio com flipflop D aps.circ as structural Verilog: 6 circuits, main circuit Relógio digital
module \Relógio_digital  (
  input  in_1,
  input  in_2,
  input  in_3,
  input  in_4,
  input  RESET
);

  wire and_1_out, BCD_7S_2_a, BCD_7S_2_b, BCD_7S_2_c, BCD_7S_2_d, BCD_7S_2_e, BCD_7S_2_f, BCD_7S_2_g,
       BCD_7S_3_a, BCD_7S_3_b, BCD_7S_3_c, BCD_7S_3_d, BCD_7S_3_e, BCD_7S_3_f, BCD_7S_3_g, BCD_7S_4_a,
       BCD_7S_4_b, BCD_7S_4_c, BCD_7S_4_d, BCD_7S_4_e, BCD_7S_4_f, BCD_7S_4_g, BCD_7S_5_a, BCD_7S_5_b,
       BCD_7S_5_c, BCD_7S_5_d, BCD_7S_5_e, BCD_7S_5_f, BCD_7S_5_g, BCD_7S_6_a, BCD_7S_6_b, BCD_7S_6_c,
       BCD_7S_6_d, BCD_7S_6_e, BCD_7S_6_f, BCD_7S_6_g, BCD_7S_a, BCD_7S_b, BCD_7S_c, BCD_7S_d, BCD_7S_e,
       BCD_7S_f, BCD_7S_g, CLK_0_5_2_vai1, CLK_0_5_vai1, CLK_0_9_2_vai1, CLK_0_9_vai1, CLK_I_vai1, CLOCK_out,
       multiplexer_1_out;
  wire [3:0] CLK_0_5_2_sa, CLK_0_5_sa, CLK_0_9_2_sa, CLK_0_9_sa, CLK_24_sa, CLK_I_sa;

  Multiplexer #(.enable("false")) multiplexer_1 (
    .in0(RESET), .in1(and_1_out), .out(multiplexer_1_out), .sel(and_1_out));
  clock_de_hora CLK_24 (
    .CLOCK(CLK_0_9_vai1), .RESET(multiplexer_1_out), .sA(CLK_24_sa[0]), .sB(CLK_24_sa[1]), .sC(CLK_24_sa[2]),
    .sD(CLK_24_sa[3]));  // open: vai1
  display BCD_7S (
    .seletor(CLK_24_sa), .a(BCD_7S_a), .b(BCD_7S_b), .c(BCD_7S_c), .d(BCD_7S_d), .e(BCD_7S_e), .f(BCD_7S_f),
    .g(BCD_7S_g));
  _7_Segment_Display u_7_segment_display_1 (
    .g(BCD_7S_g), .f(BCD_7S_f), .a(BCD_7S_a), .b(BCD_7S_b), .e(BCD_7S_e), .d(BCD_7S_d), .c(BCD_7S_c));  // open: dp
  clock_0_a_9 CLK_0_9 (
    .CLOCK(CLK_0_5_vai1), .RESET(multiplexer_1_out), .sA(CLK_0_9_sa[0]), .sB(CLK_0_9_sa[1]),
    .sC(CLK_0_9_sa[2]), .sD(CLK_0_9_sa[3]), .vai1(CLK_0_9_vai1));
  _7_Segment_Display u_7_segment_display_2 (
    .g(BCD_7S_2_g), .f(BCD_7S_2_f), .a(BCD_7S_2_a), .b(BCD_7S_2_b), .e(BCD_7S_2_e), .d(BCD_7S_2_d),
    .c(BCD_7S_2_c));  // open: dp
  and and_1 (and_1_out, BCD_7S_g, ~BCD_7S_f, BCD_7S_a, BCD_7S_b, ~BCD_7S_c, BCD_7S_d, BCD_7S_e, BCD_7S_2_f, ~BCD_7S_2_a, BCD_7S_2_g, BCD_7S_2_b, BCD_7S_2_c, ~BCD_7S_2_d, ~BCD_7S_2_e);  // AND_Gate
  display BCD_7S_2 (
    .seletor(CLK_0_9_sa), .a(BCD_7S_2_a), .b(BCD_7S_2_b), .c(BCD_7S_2_c), .d(BCD_7S_2_d), .e(BCD_7S_2_e),
    .f(BCD_7S_2_f), .g(BCD_7S_2_g));
  LED led_1 (.in(CLOCK_out));
  LED led_2 (.in(CLOCK_out));
  clock_de_0_a_5 CLK_0_5 (
    .CLOCK(CLK_0_9_2_vai1), .RESET(in_1), .sA(CLK_0_5_sa[0]), .sB(CLK_0_5_sa[1]), .sC(CLK_0_5_sa[2]),
    .sD(CLK_0_5_sa[3]), .vai1(CLK_0_5_vai1));
  _7_Segment_Display u_7_segment_display_3 (
    .g(BCD_7S_3_g), .f(BCD_7S_3_f), .a(BCD_7S_3_a), .b(BCD_7S_3_b), .e(BCD_7S_3_e), .d(BCD_7S_3_d),
    .c(BCD_7S_3_c));  // open: dp
  clock_0_a_9 CLK_0_9_2 (
    .CLOCK(CLK_0_5_2_vai1), .RESET(in_2), .sA(CLK_0_9_2_sa[0]), .sB(CLK_0_9_2_sa[1]), .sC(CLK_0_9_2_sa[2]),
    .sD(CLK_0_9_2_sa[3]), .vai1(CLK_0_9_2_vai1));
  display BCD_7S_3 (
    .seletor(CLK_0_5_sa), .a(BCD_7S_3_a), .b(BCD_7S_3_b), .c(BCD_7S_3_c), .d(BCD_7S_3_d), .e(BCD_7S_3_e),
    .f(BCD_7S_3_f), .g(BCD_7S_3_g));
  display BCD_7S_4 (
    .seletor(CLK_0_9_2_sa), .a(BCD_7S_4_a), .b(BCD_7S_4_b), .c(BCD_7S_4_c), .d(BCD_7S_4_d), .e(BCD_7S_4_e),
    .f(BCD_7S_4_f), .g(BCD_7S_4_g));
  _7_Segment_Display u_7_segment_display_4 (
    .g(BCD_7S_4_g), .f(BCD_7S_4_f), .a(BCD_7S_4_a), .b(BCD_7S_4_b), .e(BCD_7S_4_e), .d(BCD_7S_4_d),
    .c(BCD_7S_4_c));  // open: dp
  clock_de_0_a_5 CLK_0_5_2 (
    .CLOCK(CLK_I_vai1), .RESET(in_3), .sA(CLK_0_5_2_sa[0]), .sB(CLK_0_5_2_sa[1]), .sC(CLK_0_5_2_sa[2]),
    .sD(CLK_0_5_2_sa[3]), .vai1(CLK_0_5_2_vai1));
  LED led_3 (.in(CLOCK_out));
  LED led_4 (.in(CLOCK_out));
  Clock CLOCK (.out(CLOCK_out));
  clock_inicial CLK_I (
    .CLOCK(CLOCK_out), .RESET(in_4), .sA(CLK_I_sa[0]), .sB(CLK_I_sa[1]), .sC(CLK_I_sa[2]), .sD(CLK_I_sa[3]),
    .vai1(CLK_I_vai1));
  display BCD_7S_5 (
    .seletor(CLK_0_5_2_sa), .a(BCD_7S_5_a), .b(BCD_7S_5_b), .c(BCD_7S_5_c), .d(BCD_7S_5_d), .e(BCD_7S_5_e),
    .f(BCD_7S_5_f), .g(BCD_7S_5_g));
  _7_Segment_Display u_7_segment_display_5 (
    .g(BCD_7S_5_g), .f(BCD_7S_5_f), .a(BCD_7S_5_a), .b(BCD_7S_5_b), .e(BCD_7S_5_e), .d(BCD_7S_5_d),
    .c(BCD_7S_5_c));  // open: dp
  _7_Segment_Display u_7_segment_display_6 (
    .g(BCD_7S_6_g), .f(BCD_7S_6_f), .a(BCD_7S_6_a), .b(BCD_7S_6_b), .e(BCD_7S_6_e), .d(BCD_7S_6_d),
    .c(BCD_7S_6_c));  // open: dp
  display BCD_7S_6 (
    .seletor(CLK_I_sa), .a(BCD_7S_6_a), .b(BCD_7S_6_b), .c(BCD_7S_6_c), .d(BCD_7S_6_d), .e(BCD_7S_6_e),
    .f(BCD_7S_6_f), .g(BCD_7S_6_g));
endmodule

module clock_inicial (
  input  CLOCK,
  input  RESET,
  output sA,
  output sB,
  output sC,
  output sD,
  output vai1
);

  wire and_1_out, d_ff_1_q, d_ff_2_q, d_ff_3_q, d_ff_4_q;

  and and_1 (and_1_out, ~sA, sB, ~sC, sD);  // AND_Gate
  D_Flip_Flop d_ff_1 (.clk(CLOCK), .D(sA), .Q(d_ff_1_q), .preset(vai1));  // open: Qn, en, reset
  D_Flip_Flop d_ff_2 (.clk(d_ff_1_q), .D(sB), .Q(d_ff_2_q), .preset(vai1));  // open: Qn, en, reset
  D_Flip_Flop d_ff_3 (.clk(d_ff_2_q), .D(sC), .Q(d_ff_3_q), .preset(vai1));  // open: Qn, en, reset
  D_Flip_Flop d_ff_4 (.clk(d_ff_3_q), .D(sD), .Q(d_ff_4_q), .preset(vai1));  // open: Qn, en, reset
  Multiplexer #(.enable("false")) multiplexer_1 (.in0(and_1_out), .in1(RESET), .out(vai1), .sel(RESET));
  not not_1 (sA, d_ff_1_q);
  not not_2 (sB, d_ff_2_q);
  not not_3 (sC, d_ff_3_q);
  not not_4 (sD, d_ff_4_q);
endmodule

module clock_0_a_9 (
  input  CLOCK,
  input  RESET,
  output sA,
  output sB,
  output sC,
  output sD,
  output vai1
);

  wire and_1_out, d_ff_1_q, d_ff_2_q, d_ff_3_q, d_ff_4_q;

  and and_1 (and_1_out, ~sA, sB, ~sC, sD);  // AND_Gate
  D_Flip_Flop d_ff_1 (.clk(CLOCK), .D(sA), .Q(d_ff_1_q), .preset(vai1));  // open: Qn, en, reset
  D_Flip_Flop d_ff_2 (.clk(d_ff_1_q), .D(sB), .Q(d_ff_2_q), .preset(vai1));  // open: Qn, en, reset
  D_Flip_Flop d_ff_3 (.clk(d_ff_2_q), .D(sC), .Q(d_ff_3_q), .preset(vai1));  // open: Qn, en, reset
  D_Flip_Flop d_ff_4 (.clk(d_ff_3_q), .D(sD), .Q(d_ff_4_q), .preset(vai1));  // open: Qn, en, reset
  Multiplexer #(.enable("false")) multiplexer_1 (.in0(and_1_out), .in1(RESET), .out(vai1), .sel(RESET));
  not not_1 (sA, d_ff_1_q);
  not not_2 (sB, d_ff_2_q);
  not not_3 (sC, d_ff_3_q);
  not not_4 (sD, d_ff_4_q);
endmodule

module clock_de_0_a_5 (
  input  CLOCK,
  input  RESET,
  output sA,
  output sB,
  output sC,
  output sD,
  output vai1
);

  wire and_1_out, d_ff_1_q, d_ff_2_q, d_ff_3_q, d_ff_4_q;

  and and_1 (and_1_out, ~sA, sB, sC, ~sD);  // AND_Gate
  D_Flip_Flop d_ff_1 (.clk(CLOCK), .D(sA), .Q(d_ff_1_q), .preset(vai1));  // open: Qn, en, reset
  D_Flip_Flop d_ff_2 (.clk(d_ff_1_q), .D(sB), .Q(d_ff_2_q), .preset(vai1));  // open: Qn, en, reset
  D_Flip_Flop d_ff_3 (.clk(d_ff_2_q), .D(sC), .Q(d_ff_3_q), .preset(vai1));  // open: Qn, en, reset
  D_Flip_Flop d_ff_4 (.clk(d_ff_3_q), .D(sD), .Q(d_ff_4_q), .preset(vai1));  // open: Qn, en, reset
  Multiplexer #(.enable("false")) multiplexer_1 (.in0(and_1_out), .in1(RESET), .out(vai1), .sel(RESET));
  not not_1 (sA, d_ff_1_q);
  not not_2 (sB, d_ff_2_q);
  not not_3 (sC, d_ff_3_q);
  not not_4 (sD, d_ff_4_q);
endmodule

module display (
  input  [3:0] seletor,
  output a,
  output b,
  output c,
  output d,
  output e,
  output f,
  output g
);

  Multiplexer #(.select(4), .enable("false")) multiplexer_1 (
    .in0(1'b1), .in1(1'b0), .in2(1'b1), .in3(1'b1), .in4(1'b0), .in5(1'b1), .in6(1'b1), .in7(1'b1),
    .in8(1'b1), .in9(1'b1), .out(a), .sel(seletor));  // open: in10, in11, in12, in13, in14, in15
  Multiplexer #(.select(4), .enable("false")) multiplexer_2 (
    .in0(1'b1), .in1(1'b1), .in2(1'b0), .in3(1'b1), .in4(1'b1), .in5(1'b1), .in6(1'b1), .in7(1'b1),
    .in8(1'b1), .in9(1'b1), .out(c), .sel(seletor));  // open: in10, in11, in12, in13, in14, in15
  Multiplexer #(.select(4), .enable("false")) multiplexer_3 (
    .in0(1'b1), .in1(1'b0), .in2(1'b1), .in3(1'b0), .in4(1'b0), .in5(1'b0), .in6(1'b1), .in7(1'b0),
    .in8(1'b1), .in9(1'b0), .out(e), .sel(seletor));  // open: in10, in11, in12, in13, in14, in15
  Multiplexer #(.select(4), .enable("false")) multiplexer_4 (
    .in0(1'b0), .in1(1'b0), .in2(1'b1), .in3(1'b1), .in4(1'b1), .in5(1'b1), .in6(1'b1), .in7(1'b0),
    .in8(1'b1), .in9(1'b1), .in10(1'b0), .out(g), .sel(seletor));  // open: in11, in12, in13, in14, in15
  Multiplexer #(.select(4), .enable("false")) multiplexer_5 (
    .in0(1'b1), .in1(1'b1), .in2(1'b1), .in3(1'b1), .in4(1'b1), .in5(1'b0), .in6(1'b0), .in7(1'b1),
    .in8(1'b1), .in9(1'b1), .in10(1'b0), .out(b), .sel(seletor));  // open: in11, in12, in13, in14, in15
  Multiplexer #(.select(4), .enable("false")) multiplexer_6 (
    .in0(1'b1), .in1(1'b0), .in2(1'b1), .in3(1'b1), .in4(1'b0), .in5(1'b1), .in6(1'b1), .in7(1'b0),
    .in8(1'b1), .in9(1'b1), .in10(1'b1), .out(d), .sel(seletor));  // open: in11, in12, in13, in14, in15
  Multiplexer #(.select(4), .enable("false")) multiplexer_7 (
    .in0(1'b1), .in1(1'b0), .in2(1'b0), .in3(1'b0), .in4(1'b1), .in5(1'b1), .in6(1'b1), .in7(1'b0),
    .in8(1'b1), .in9(1'b1), .in10(1'b0), .out(f), .sel(seletor));  // open: in11, in12, in13, in14, in15
endmodule

module clock_de_hora (
  input  CLOCK,
  input  RESET,
  output sA,
  output sB,
  output sC,
  output sD,
  output vai1
);

  wire and_1_out, d_ff_1_q, d_ff_2_q, d_ff_3_q, d_ff_4_q;

  and and_1 (and_1_out, ~sA, ~sB, sC, sD);  // AND_Gate
  D_Flip_Flop d_ff_1 (.clk(CLOCK), .D(sA), .Q(d_ff_1_q), .preset(vai1));  // open: Qn, en, reset
  D_Flip_Flop d_ff_2 (.clk(d_ff_1_q), .D(sB), .Q(d_ff_2_q), .preset(vai1));  // open: Qn, en, reset
  D_Flip_Flop d_ff_3 (.clk(d_ff_2_q), .D(sC), .Q(d_ff_3_q), .preset(vai1));  // open: Qn, en, reset
  D_Flip_Flop d_ff_4 (.clk(d_ff_3_q), .D(sD), .Q(d_ff_4_q), .preset(vai1));  // open: Qn, en, reset
  Multiplexer #(.enable("false")) multiplexer_1 (.in0(and_1_out), .in1(RESET), .out(vai1), .sel(RESET));
  not not_1 (sA, d_ff_1_q);
  not not_2 (sB, d_ff_2_q);
  not not_3 (sC, d_ff_3_q);
  not not_4 (sD, d_ff_4_q);
endmodule
